// Logisim project matrixv2.circ as structural Verilog: 1 circuit, main circuit main
module main (
  input  in_1,
  input  [7:0] in_2,
  input  in_3,
  input  in_4,
  input  in_5,
  input  in_6,
  input  in_7,
  input  in_8,
  input  [2:0] in_9,
  input  in_10,
  input  in_11,
  input  in_12,
  input  in_13,
  input  in_14,
  input  in_15,
  input  in_16
);

  wire clock_1_out, demultiplexer_2_out0, demultiplexer_2_out1, demultiplexer_2_out2, demultiplexer_2_out3,
       demultiplexer_2_out4, demultiplexer_2_out5, demultiplexer_2_out6, demultiplexer_2_out7;
  wire [2:0] counter_2_q;
  wire [7:0] counter_1_q, demultiplexer_1_out0, demultiplexer_1_out1, demultiplexer_1_out2,
       demultiplexer_1_out3, demultiplexer_1_out4, demultiplexer_1_out5, demultiplexer_1_out6,
       demultiplexer_1_out7, register_1_q, register_2_q, register_3_q, register_4_q, register_5_q,
       register_6_q, register_7_q, register_8_q, rom_1_data, undriven;

  // Probe on undriven[0]
  // Probe on undriven[1]
  // Probe on undriven[2]
  // Probe on undriven[3]
  // Probe on undriven[4]
  // Probe on undriven[5]
  // Probe on undriven[6]
  // Probe on undriven[7]
  Clock clock_1 (.out(clock_1_out));
  Counter #(.max('h5f), .trigger("falling")) counter_1 (
    .load(in_1), .D(in_2), .count(in_3), .Q(counter_1_q), .clk(clock_1_out));  // open: carry, clr
  Counter #(.width(3), .max('h7), .trigger("falling")) counter_2 (
    .load(in_6), .D(in_9), .count(in_10), .Q(counter_2_q), .clk(clock_1_out));  // open: carry, clr
  Demultiplexer #(.select(3), .width(8), .disabled(0)) demultiplexer_1 (
    .out0(demultiplexer_1_out0), .out1(demultiplexer_1_out1), .out2(demultiplexer_1_out2),
    .out3(demultiplexer_1_out3), .out4(demultiplexer_1_out4), .out5(demultiplexer_1_out5),
    .out6(demultiplexer_1_out6), .out7(demultiplexer_1_out7), .in(rom_1_data), .sel(counter_2_q), .en(in_13));
  Register register_1 (
    .D(demultiplexer_1_out0), .Q(register_1_q), .clk(demultiplexer_2_out0), .clr(in_16));  // open: en
  ROM rom_1 (.addr(counter_1_q), .data(rom_1_data));  // open: sel
  DotMatrix #(.matrixcols(8), .matrixrows(8)) dotmatrix_1 (
    .col0(register_1_q), .col1(register_2_q), .col2(register_3_q), .col3(register_5_q), .col4(register_4_q),
    .col5(register_6_q), .col6(register_7_q), .col7(register_8_q));
  Register register_2 (
    .D(demultiplexer_1_out1), .Q(register_2_q), .clk(demultiplexer_2_out1), .clr(in_16));  // open: en
  Register register_3 (
    .D(demultiplexer_1_out2), .Q(register_3_q), .clk(demultiplexer_2_out2), .clr(in_16));  // open: en
  Demultiplexer #(.select(3), .disabled(0)) demultiplexer_2 (
    .out0(demultiplexer_2_out0), .out1(demultiplexer_2_out1), .out2(demultiplexer_2_out2),
    .out3(demultiplexer_2_out3), .out4(demultiplexer_2_out4), .out5(demultiplexer_2_out5),
    .out6(demultiplexer_2_out6), .out7(demultiplexer_2_out7), .in(clock_1_out), .sel(counter_2_q), .en(in_13));
  Register register_4 (
    .D(demultiplexer_1_out4), .Q(register_4_q), .clk(demultiplexer_2_out4), .clr(in_16));  // open: en
  Register register_5 (
    .D(demultiplexer_1_out3), .Q(register_5_q), .clk(demultiplexer_2_out3), .clr(in_16));  // open: en
  Register register_6 (
    .D(demultiplexer_1_out5), .Q(register_6_q), .clk(demultiplexer_2_out5), .clr(in_16));  // open: en
  Register register_7 (
    .D(demultiplexer_1_out6), .Q(register_7_q), .clk(demultiplexer_2_out6), .clr(in_16));  // open: en
  Register register_8 (
    .D(demultiplexer_1_out7), .Q(register_8_q), .clk(demultiplexer_2_out7), .clr(in_16));  // open: en

  // Notes on the sheet:
  //   contents of rom_1 (hex, n*v repeats v):
  //   0 3f 7f 48 48 7f 3f 10*0 7f 7f 49 49 7f 36 10*0 3e 7f 41 41 63 22 10*0 7f 7f 41 41 7f 3e 10*0 7f 7f
  //   49 49 49 41 10*0 7f 7f 48 48 48 40
endmodule
